# Fritzing sketch Door Sign Fritzing (saved by Fritzing 0.9.0b)
breadboards: 1

parts:
  Part1 = Spark Core (v1.0)
  IC1 = Voltage Regulator [package=to220-igo]
  VCC1 = Battery block 9V
  J1 = female pin header, 4 pins [form="♀ (female)"]

nets:
  N1: Part1.GND, IC1.IN, VCC1.-, J1.pin4
  N2: Part1.VIN, IC1.OUT, J1.pin3
  N3: Part1.D0, J1.pin2
  N4: Part1.D1, J1.pin1
  N5: IC1.GND, VCC1.+
